// Digital circuit Mips32SoC.dig as structural Verilog
module Mips32SoC (
  input  clk,
  input  rst
);

  wire ALUSrc, and_1_out, and_2_out, ImmExt, InvOpcode, Jump, MemRead, MemWrite, not_1_out, or_1_out, RegDst,
       RegWrite, zero;
  wire [1:0] Branch, MemToReg;
  wire [2:0] control_unit_full_1_alufunc;
  wire [3:0] add_1_s_2;
  wire [4:0] multiplexer_2_out;
  wire [5:0] func;
  wire [7:0] alu_1_p4_2, PC_q_2;
  wire [25:6] InstMem_d;
  wire [27:0] add_1_s;
  wire [31:0] add_2_s, alu_1_p4, bitextender_1_out, DataMem_d, multiplexer_1_out, multiplexer_3_out,
       multiplexer_4_out, multiplexer_5_out, multiplexer_6_out, multiplexer_7_out, PC_q, registerfile_1_da,
       registerfile_1_db;
  wire [31:26] InstMem_d_2;

  Multiplexer #(.Bits(32)) multiplexer_1 (
    .sel(rst), .in_0(multiplexer_7_out), .in_1({32{1'b0}}), .out(multiplexer_1_out));
  Register #(.Bits(32)) PC (.D(multiplexer_1_out), .C(clk), .en(1'b1), .Q({PC_q[31:10], PC_q_2, PC_q[1:0]}));
  Add #(.Bits(32)) add_1 (
    .a({PC_q[31:10], PC_q_2, PC_q[1:0]}), .b(32'h4), .c_i(1'b0), .s({add_1_s_2, add_1_s}));  // open: c_o
  ROM #(.AddrBits(8), .Bits(32)) InstMem (.A(PC_q_2), .sel(1'b1), .D({InstMem_d_2, InstMem_d, func}));
  Multiplexer #(.Bits(5)) multiplexer_2 (
    .sel(RegDst), .in_0(InstMem_d[20:16]), .in_1(InstMem_d[15:11]), .out(multiplexer_2_out));
  control_unit_full control_unit_full_1 (
    .opcode(InstMem_d_2), .\function (func), .jump(Jump), .Branch(Branch), .MemRead(MemRead),
    .MemWrite(MemWrite), .MemToReg(MemToReg), .ALUSrc(ALUSrc), .RegWrite(RegWrite), .RegDst(RegDst),
    .InvOpcode(InvOpcode), .ALUFunc(control_unit_full_1_alufunc), .ImmExtend(ImmExt));
  BitExtender #(.inputBits(16), .outputBits(32)) bitextender_1 (.in({InstMem_d[15:6], func}), .out(bitextender_1_out));
  RegisterFile #(.AddrBits(5), .Bits(32)) registerfile_1 (
    .Din(multiplexer_5_out), .we(RegWrite), .Rw(multiplexer_2_out), .C(clk), .Ra(InstMem_d[25:21]),
    .Rb(InstMem_d[20:16]), .Da(registerfile_1_da), .Db(registerfile_1_db));
  Multiplexer #(.Bits(32)) multiplexer_3 (
    .sel(ImmExt), .in_0({{16{1'b0}}, InstMem_d[15:6], func}), .in_1(bitextender_1_out),
    .out(multiplexer_3_out));
  Multiplexer #(.Bits(32)) multiplexer_4 (
    .sel(ALUSrc), .in_0(registerfile_1_db), .in_1(multiplexer_3_out), .out(multiplexer_4_out));
  // alu alu_1: pin names not known; wires that end beside it: registerfile_1_da, multiplexer_4_out, control_unit_full_1_alufunc, {alu_1_p4[31:10], alu_1_p4_2, alu_1_p4[1:0]}, zero
  not not_1 (not_1_out, zero);
  and and_1 (and_1_out, Branch[0], zero);
  and and_2 (and_2_out, Branch[1], not_1_out);
  Multiplexer #(.Selector_Bits(2), .Bits(32)) multiplexer_5 (
    .sel(MemToReg), .in_0({alu_1_p4[31:10], alu_1_p4_2, alu_1_p4[1:0]}), .in_1(DataMem_d),
    .in_2({{16{1'b0}}, InstMem_d[15:6], func}), .in_3({32{1'b0}}), .out(multiplexer_5_out));
  RAMDualPort #(.AddrBits(8), .Bits(32)) DataMem (
    .A(alu_1_p4_2), .Din(registerfile_1_db), .str(MemWrite), .C(clk), .ld(MemRead), .D(DataMem_d));
  Add #(.Bits(32)) add_2 (
    .a({add_1_s_2, add_1_s}), .b({multiplexer_3_out[29:0], 2'b00}), .c_i(1'b0), .s(add_2_s));  // open: c_o
  or or_1 (or_1_out, and_1_out, and_2_out);
  Multiplexer #(.Bits(32)) multiplexer_6 (
    .sel(or_1_out), .in_0({add_1_s_2, add_1_s}), .in_1(add_2_s), .out(multiplexer_6_out));
  Multiplexer #(.Bits(32)) multiplexer_7 (
    .sel(Jump), .in_0(multiplexer_6_out), .in_1({add_1_s_2, InstMem_d, func, 2'b00}), .out(multiplexer_7_out));

  // Notes on the sheet:
  //   contents of InstMem (hex, n*v repeats v):
  //   deadbeef,11111111,22222222,33333333,44444444,55555555,66666666,77777777,88888888,
  //   99999999
endmodule
